# Fritzing sketch Servo (saved by Fritzing 0.9.3b)
breadboards: 1

parts:
  WeMos_D1_Mini1 = WeMos D1 Mini
  S1 = Round Pushbutton
  S2 = Round Pushbutton
  S3 = Toggle Switch [package=THT]
  S4 = Toggle Switch [package=THT]
  J1 = Basic Servo
  R1 = Resistor [tolerance=±5% resistance=220 package="0805 [SMD]"]
  R2 = Resistor [tolerance=±5% resistance=220 package="0805 [SMD]"]
  R3 = Resistor [tolerance=±5% resistance=220 package="0805 [SMD]"]
  R4 = Resistor [tolerance=±5% resistance=220 package="0805 [SMD]"]
  WeMos_D1_Mini_Relay_Shield_V1 = WeMos D1 Mini Relay Shield V2

nets:
  5V: WeMos_D1_Mini1.5V, WeMos_D1_Mini1.D6, S2.leg1, S3.COM, S4.L2, J1.vcc, R1.Pin_0, WeMos_D1_Mini_Relay_Shield_V1.5V
  N1: WeMos_D1_Mini1.D1, WeMos_D1_Mini_Relay_Shield_V1.D1
  N2: WeMos_D1_Mini1.D4, J1.pulse
  N3: WeMos_D1_Mini1.D5, WeMos_D1_Mini1.G, S1.leg1, J1.gnd, R2.Pin_0, R3.Pin_0, R4.Pin_1, WeMos_D1_Mini_Relay_Shield_V1.G
  N4: WeMos_D1_Mini1.D7, S3.L2, R3.Pin_1
  N5: WeMos_D1_Mini1.D8, S4.COM, R4.Pin_0
  N6: S1.leg0, R1.Pin_1
  N7: S2.leg0, R2.Pin_1
